# Fritzing sketch 第2课LED与按键 (saved by Fritzing 1.0.5)
breadboards: 1

parts:
  元件1 = Arduino Uno (Rev3)  # not connected
  LED1 = LED - 5mm [color="Red (633nm)" current=0.030A package="5 mm [THT]"]
  R1 = Resistor [tolerance=±5% power=0.25W resistance=220 package=THT]
  S1 = Pushbutton [package="[THT]"]

nets:
  N1: LED1.anode, R1.Pin_1
  N2: R1.Pin_0, S1.Pin_3, S1.Pin_4
  N3: S1.Pin_1, S1.Pin_2

custom parts:
  Arduino Uno (Rev3): The Arduino Uno is a microcontroller board based on the ATmega328 (datasheet). It has 14 digital input/output pins (of which 6 can be used as PWM outputs), 6 analog inputs, a 16 MHz ceramic resonator, a USB connection, a power jack, an ICSP header, and a reset button. It contains everything needed to support the microcontroller; simply connect it to a computer with a USB cable or power it with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
