# Fritzing sketch 流水灯 (saved by Fritzing 1.0.5)

parts:
  Grove1 = Grove 3 Axis Digital Accelerometer 16g
  元件1 = Arduino Uno (Rev3)
  TRAF1 = YANGUILE

nets:
  N1: Grove1.GND, 元件1.GND#117
  VCC: Grove1.VCC, 元件1.5V
  N2: Grove1.RX, 元件1.D6
  N3: Grove1.TX, 元件1.D5
  N4: 元件1.D2, TRAF1.R
  N5: 元件1.D3, TRAF1.Y
  N6: 元件1.D4, TRAF1.G
  N7: 元件1.GND#86, TRAF1.GND

custom parts:
  Grove 3 Axis Digital Accelerometer 16g: A 3 axis digital accelerometer (16g)
  Arduino Uno (Rev3): The Arduino Uno is a microcontroller board based on the ATmega328 (datasheet). It has 14 digital input/output pins (of which 6 can be used as PWM outputs), 6 analog inputs, a 16 MHz ceramic resonator, a USB connection, a power jack, an ICSP header, and a reset button. It contains everything needed to support the microcontroller; simply connect it to a computer with a USB cable or power it with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
  YANGUILE: TRAF
