# Fritzing sketch 世界那么大 (saved by Fritzing 1.0.5)

parts:
  元件1 = Arduino Uno (Rev3)
  VOICE1 = YANGUILE

nets:
  N1: 元件1.D9, VOICE1.RST
  N2: 元件1.D10, VOICE1.DATA
  N3: 元件1.D11, VOICE1.BUSY

custom parts:
  Arduino Uno (Rev3): The Arduino Uno is a microcontroller board based on the ATmega328 (datasheet). It has 14 digital input/output pins (of which 6 can be used as PWM outputs), 6 analog inputs, a 16 MHz ceramic resonator, a USB connection, a power jack, an ICSP header, and a reset button. It contains everything needed to support the microcontroller; simply connect it to a computer with a USB cable or power it with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
  YANGUILE: VOICE
